// Logisim project AluBebe.circ as structural Verilog: 6 circuits, main circuit Alu
module Alu (
  input  [7:0] N,
  input  [7:0] R0,
  input  [7:0] R1,
  input  [3:0] Banderas,
  input  [4:0] Instrucciones,
  output [7:0] ACC,
  output [7:0] ACC2,
  output [3:0] BanderasOut
);

  wire [19:0] adc_1_salida, add_1_salida, sbb_1_salida, sub_1_salida, xchg_1_salida;

  xchg xchg_1 (.Entrada({Banderas, R1, R0, N}), .Salida(xchg_1_salida));
  add add_1 (.Entrada({Banderas, R1, R0, N}), .Salida(add_1_salida));
  adc adc_1 (.Entrada({Banderas, R1, R0, N}), .Salida(adc_1_salida));
  sub sub_1 (.Entrada({Banderas, R1, R0, N}), .Salida(sub_1_salida));
  sbb sbb_1 (.Entrada({Banderas, R1, R0, N}), .Salida(sbb_1_salida));
  Multiplexer #(.select(5), .width(20)) multiplexer_1 (
    .in0(xchg_1_salida), .in2(add_1_salida), .in3(adc_1_salida), .in4(sub_1_salida), .in5(sbb_1_salida),
    .out({BanderasOut, ACC2, ACC}), .sel(Instrucciones));  // open: in1, in6, in7, in8, in9, in10, in11, in12, in13, in14, in15, in16, in17, in18, in19, in20, in21, in22, in23, in24, in25, in26, in27, in28, in29, in30, in31

  // Notes on the sheet:
  //   C O S Z
endmodule

module add (
  input  [27:0] Entrada,
  output [19:0] Salida
);

  wire xnor_1_out, xor_1_out;

  Adder adder_1 (.a(Entrada[7:0]), .b(Entrada[15:8]), .out({Salida[17], Salida[6:0]}), .cin(1'b0), .cout(Salida[19]));
  xor xor_1 (xor_1_out, Salida[17], Entrada[7]);
  xnor xnor_1 (xnor_1_out, Entrada[7], Entrada[15]);
  nor nor_1 (Salida[16], Salida[0], Salida[1], Salida[2], Salida[3], Salida[4], Salida[5], Salida[6], Salida[17]);
  and and_1 (Salida[18], xor_1_out, xnor_1_out);

  assign Salida[15:7] = {Entrada[23:16], Salida[17]};

  // Notes on the sheet:
  //   N
  //   R0
  //   R1
  //   acc
  //   acc2
  //   cosz
endmodule

module xchg (
  input  [27:0] Entrada,
  output [19:0] Salida
);


  assign Salida = {Entrada[27:24], Entrada[15:8], Entrada[23:16]};

  // Notes on the sheet:
  //   N
  //   BANDERAS
  //   R0 -> ACC2
  //   R1 -> ACC
endmodule

module adc (
  input  [27:0] Entrada,
  output [19:0] Salida
);

  wire xnor_1_out, xor_1_out;

  Adder adder_1 (
    .a(Entrada[7:0]), .b(Entrada[15:8]), .out({Salida[17], Salida[6:0]}), .cin(Entrada[27]), .cout(Salida[19]));
  xor xor_1 (xor_1_out, Salida[17], Entrada[7]);
  xnor xnor_1 (xnor_1_out, Entrada[7], Entrada[15]);
  nor nor_1 (Salida[16], Salida[0], Salida[1], Salida[2], Salida[3], Salida[4], Salida[5], Salida[6], Salida[17]);
  and and_1 (Salida[18], xor_1_out, xnor_1_out);

  assign Salida[15:7] = {Entrada[23:16], Salida[17]};

  // Notes on the sheet:
  //   N
  //   R0
  //   R1
  //   acc
  //   acc2
  //   cosz
endmodule

module sub (
  input  [27:0] Entrada,
  output [19:0] Salida
);

  wire and_1_out, and_2_out, comparator_1_gt, comparator_1_lt, comparator_2_gt, comparator_2_lt,
       comparator_3_gt, comparator_3_lt;

  Subtractor subtractor_1 (
    .a(Entrada[15:8]), .b(Entrada[7:0]), .out({Salida[17], Salida[6:0]}), .bin(1'b0), .bout(Salida[19]));
  nor nor_1 (Salida[16], Salida[0], Salida[1], Salida[2], Salida[3], Salida[4], Salida[5], Salida[6], Salida[17]);
  Comparator comparator_1 (
    .a({Salida[17], Salida[6:0]}), .b({8{1'b0}}), .gt(comparator_1_gt), .lt(comparator_1_lt));  // open: eq
  Comparator comparator_2 (.a(Entrada[7:0]), .b({8{1'b0}}), .gt(comparator_2_gt), .lt(comparator_2_lt));  // open: eq
  Comparator comparator_3 (.a(Entrada[15:8]), .b({8{1'b0}}), .gt(comparator_3_gt), .lt(comparator_3_lt));  // open: eq
  and and_1 (and_1_out, comparator_1_lt, comparator_2_gt, comparator_3_lt);
  and and_2 (and_2_out, comparator_1_gt, comparator_2_lt, comparator_3_gt);
  or or_1 (Salida[18], and_1_out, and_2_out);

  assign Salida[15:7] = {Entrada[23:16], Salida[17]};

  // Notes on the sheet:
  //   N
  //   R0
  //   R1
  //   acc
  //   acc2
  //   t
  //   b
  //   a
  //   cosz
endmodule

module sbb (
  input  [27:0] Entrada,
  output [19:0] Salida
);

  wire and_1_out, and_2_out, comparator_1_gt, comparator_1_lt, comparator_2_gt, comparator_2_lt,
       comparator_3_gt, comparator_3_lt;

  Subtractor subtractor_1 (
    .a(Entrada[15:8]), .b(Entrada[7:0]), .out({Salida[17], Salida[6:0]}), .bin(Entrada[27]), .bout(Salida[19]));
  nor nor_1 (Salida[16], Salida[0], Salida[1], Salida[2], Salida[3], Salida[4], Salida[5], Salida[6], Salida[17]);
  Comparator comparator_1 (
    .a({Salida[17], Salida[6:0]}), .b({8{1'b0}}), .gt(comparator_1_gt), .lt(comparator_1_lt));  // open: eq
  Comparator comparator_2 (.a(Entrada[7:0]), .b({8{1'b0}}), .gt(comparator_2_gt), .lt(comparator_2_lt));  // open: eq
  Comparator comparator_3 (.a(Entrada[15:8]), .b({8{1'b0}}), .gt(comparator_3_gt), .lt(comparator_3_lt));  // open: eq
  and and_1 (and_1_out, comparator_1_lt, comparator_2_gt, comparator_3_lt);
  and and_2 (and_2_out, comparator_1_gt, comparator_2_lt, comparator_3_gt);
  or or_1 (Salida[18], and_1_out, and_2_out);

  assign Salida[15:7] = {Entrada[23:16], Salida[17]};

  // Notes on the sheet:
  //   N
  //   R0
  //   R1
  //   acc
  //   acc2
  //   t
  //   b
  //   a
  //   cosz
endmodule
